# Fritzing sketch schematic (saved by Fritzing 0.8.5b)
breadboards: 1

parts:
  Arduino_Uno = Arduino Uno (Rev3)
  Part2 = SRF05 Ultrasonic Rangefinder
  XBee1 = XBEE-1 [package=xbee-1_lock]
  Raspberry_Pi_B_rev1 = Raspberry Pi B rev2
  J1 = Piezo Speaker

nets:
  N1: Arduino_Uno.D11_PWM/MOSI, J1.pin2
  N2: Arduino_Uno.D12/MISO, Part2.Echo
  N3: Arduino_Uno.D13/SCK, Part2.Trig
  GND: Arduino_Uno.GND, Part2.GND, J1.pin1
  5V: Arduino_Uno.5V, Part2.VCC
  VDD: XBee1.VDD, Raspberry_Pi_B_rev1.3V3
  N4: XBee1.DOUT, Raspberry_Pi_B_rev1.GPIO_15
  GND_2: XBee1.GND, Raspberry_Pi_B_rev1.GND
